// Logisim project X64000.circ as structural Verilog: 2 circuits, main circuit ResetUnit
module ResetUnit (
  input  ResetIssue,
  output [15:0] ResetMagic
);

  and and_1 (ResetMagic[9], ResetIssue, 1'b1);
  not not_1 (ResetMagic[15], ResetMagic[9]);

  assign {ResetMagic[14:10], ResetMagic[8:0]} = {{7{ResetMagic[15]}}, ResetMagic[9], ResetMagic[15], ResetMagic[9], ResetMagic[15], ResetMagic[9], ResetMagic[15], ResetMagic[9]};

  // Other names for the same wires on the sheet: RST[15:0] = {{6{ResetMagic[15]}}, ResetMagic[9], {2{ResetMagic[15]}}, ResetMagic[9], ResetMagic[15], ResetMagic[9], ResetMagic[15], ResetMagic[9], ResetMagic[15], ResetMagic[9]}

  // Notes on the sheet:
  //   32k reset line
endmodule

module RegisterUnit (
  input  [63:0] RegisterValue,
  input  [7:0] RegisterIndex,
  output [7:0] RegisterIndexValue,
  output [63:0] RegisterOutputValue
);

  wire Clk_out, RegEnable, RegWrite, undriven, undriven_2, xor_1_out, xor_2_out, xor_3_out, xor_4_out,
       xor_5_out, xor_6_out;

  and and_1 (RegWrite, RegEnable, 1'b1);
  Register #(.width(64)) register_1 (
    .D(RegisterValue), .en(RegWrite), .clk(Clk_out), .Q(RegisterOutputValue), .clr(undriven));
  // NoConnect on undriven
  xor xor_1 (xor_1_out, RegisterIndex[0], RegisterIndex[1]);
  xor xor_2 (xor_2_out, RegisterIndex[2], RegisterIndex[3]);
  xor xor_3 (xor_3_out, RegisterIndex[4], RegisterIndex[5]);
  xor xor_4 (xor_4_out, RegisterIndex[6], RegisterIndex[7]);
  Clock Clk (.out(Clk_out));
  xor xor_5 (xor_5_out, xor_1_out, xor_2_out);
  xor xor_6 (xor_6_out, xor_3_out, xor_4_out);
  Register IndexRegister (.D(RegisterIndex), .en(RegWrite), .clk(Clk_out), .Q(RegisterIndexValue), .clr(undriven_2));
  // NoConnect on undriven_2
  xor xor_7 (RegEnable, xor_5_out, xor_6_out);

  // Other names for the same wires on the sheet: RegisterValueTunnel[63:0] = RegisterValue

  // Notes on the sheet:
  //   32k register file
  //   we get the index and put inside
  //   this register
  //   This is like an array
endmodule
